// Logisim project control_logic.circ as structural Verilog: 1 circuit, main circuit control_logic
module control_logic (
  input  [31:0] inst,
  input  BrEq,
  input  BrLt,
  output PCSel,
  output RegWEn,
  output [2:0] ImmSel,
  output BrUn,
  output ASel,
  output BSel,
  output [3:0] ALUSel,
  output MemRW,
  output [1:0] WBSel,
  output CSRSel,
  output CSRWen
);

  wire d25, d30, is101, isAuipc, isBranch, isCsr, isI, isJal, isJalr, isLoad, isLui, isR, isStore, not_1_out,
       or_1_out, or_5_out, or_6_out, useArith, valid;
  wire [3:0] ALUSel_arith, multiplexer_1_out, multiplexer_2_out, multiplexer_3_out, multiplexer_4_out,
       multiplexer_5_out;

  and and_1 (valid, inst[0], inst[1]);
  Multiplexer #(.enable("false"), .width(4)) multiplexer_1 (
    .in0(4'b0000), .in1(4'b1101), .out(multiplexer_1_out), .sel(isLui));
  not not_1 (not_1_out, inst[13]);
  and and_2 (d25, inst[25], isR);
  or or_1 (or_1_out, isR, is101);
  Multiplexer #(.enable("false"), .select(3), .width(4)) multiplexer_2 (
    .in0(4'b0000), .in1(4'b0110), .in2(4'b0111), .in3(4'b0000), .in4(4'b0011), .in5(4'b0100), .in6(4'b0010),
    .in7(4'b0001), .out(multiplexer_2_out), .sel(inst[14:12]));
  Multiplexer #(.enable("false"), .select(3), .width(4)) multiplexer_3 (
    .in0(4'b1100), .in1(4'b0000), .in2(4'b0000), .in3(4'b0000), .in4(4'b0000), .in5(4'b0101), .in6(4'b0000),
    .in7(4'b0000), .out(multiplexer_3_out), .sel(inst[14:12]));
  and and_3 (is101, inst[12], not_1_out, inst[14]);
  and and_4 (d30, inst[30], or_1_out);
  Multiplexer #(.enable("false"), .width(4)) multiplexer_4 (
    .in0(multiplexer_2_out), .in1(multiplexer_3_out), .out(multiplexer_4_out), .sel(d30));
  Multiplexer #(.enable("false"), .select(3), .width(4)) multiplexer_5 (
    .in0(4'b1010), .in1(4'b1110), .in2(4'b0000), .in3(4'b1011), .in4(4'b0000), .in5(4'b0000), .in6(4'b0000),
    .in7(4'b0000), .out(multiplexer_5_out), .sel(inst[14:12]));
  or or_2 (useArith, isR, isI);
  Multiplexer #(.enable("false"), .width(4)) multiplexer_6 (
    .in0(multiplexer_1_out), .in1(ALUSel_arith), .out(ALUSel), .sel(useArith));
  Multiplexer #(.enable("false"), .width(4)) multiplexer_7 (
    .in0(multiplexer_4_out), .in1(multiplexer_5_out), .out(ALUSel_arith), .sel(d25));
  Decoder #(.select(5)) decoder_1 (
    .out0(isLoad), .out4(isI), .out5(isAuipc), .out8(isStore), .out12(isR), .out13(isLui), .out24(isBranch),
    .out25(isJalr), .out27(isJal), .out28(isCsr), .sel(inst[6:2]), .en(valid));  // open: out1, out2, out3, out6, out7, out9, out10, out11, out14, out15, out16, out17, out18, out19, out20, out21, out22, out23, out26, out29, out30, out31
  or or_3 (RegWEn, isR, isI, isLui, isAuipc);
  or or_4 (ASel, isAuipc, isBranch, isJal);
  or or_5 (or_5_out, isR, isBranch);
  or or_6 (or_6_out, isLui, isAuipc);
  not not_2 (BSel, or_5_out);
  Multiplexer #(.enable("false"), .width(3)) multiplexer_8 (.in0(3'b000), .in1(3'b011), .out(ImmSel), .sel(or_6_out));

  assign BrUn = 1'b0;
  assign CSRSel = 1'b0;
  assign CSRWen = 1'b0;
  assign MemRW = 1'b0;
  assign PCSel = 1'b0;
  assign WBSel = 2'b00;

  // Other names for the same wires on the sheet: opcode[4:0] = inst[6:2]; func3[2:0] = inst[14:12]; raw25 = inst[25];
  //   raw30 = inst[30]

  // Notes on the sheet:
  //   INPUTS to your circuit
  //   DON'T CHANGE THE LOCATIONS OF THE INPUTS AND OUTPUTS!
  //   OUTPUT from your circuit
endmodule
