// Logisim project cpu.circ as structural Verilog: 1 circuit, main circuit cpu
module cpu (
  input  clk,
  input  [31:0] INSTRUCTION,
  input  [31:0] READ_DATA,
  output [31:0] WRITE_ADDRESS,
  output [31:0] PROGRAM_COUNTER,
  output [31:0] ra,
  output [31:0] sp,
  output [31:0] t0,
  output [31:0] t1,
  output [31:0] t2,
  output [31:0] s0,
  output [31:0] s1,
  output [31:0] a0,
  output [31:0] tohost,
  output [3:0] WRITE_ENABLE,
  output [31:0] WRITE_DATA
);

  wire ASel, BrEq, BrLt, BrUn, BSel, CSRSel, CSRWen, LB, LH, MemRW, PCSel, RegWEn, SB, SH, undriven,
       undriven_2;
  wire [1:0] WBSel;
  wire [2:0] func3, ImmSel;
  wire [3:0] ALUSel, multiplexer_5_out, multiplexer_6_out;
  wire [6:0] func7;
  wire [24:0] inst_ex;
  wire [31:0] adder_1_out, adder_2_out, ALU_A, ALU_B, bit_extender_1_out, bit_extender_2_out, Imm0,
       multiplexer_1_out, multiplexer_2_out, multiplexer_7_out, multiplexer_9_out, pc_ex, r1, READ_DATA2, wb;

  Adder #(.width(32)) adder_1 (.a(PROGRAM_COUNTER), .b(32'h4), .out(adder_1_out));  // open: cin, cout
  Multiplexer #(.enable("false"), .width(32)) multiplexer_1 (
    .in0(adder_1_out), .in1(WRITE_ADDRESS), .out(multiplexer_1_out), .sel(PCSel));
  Register #(.width(32)) PC (.D(multiplexer_1_out), .en(undriven), .clk(clk), .Q(PROGRAM_COUNTER));  // open: clr
  Register #(.width(32)) register_1 (.D(PROGRAM_COUNTER), .en(undriven_2), .clk(clk), .Q(pc_ex));  // open: clr
  Multiplexer #(.enable("false"), .width(32)) multiplexer_2 (
    .in0(INSTRUCTION), .in1(32'h13), .out(multiplexer_2_out), .sel(PCSel));
  Register #(.width(32)) register_2 (
    .D(multiplexer_2_out), .clk(clk), .Q({func7, inst_ex[24:15], func3, inst_ex[11:0]}));  // open: en, clr
  imm_gen imm_gen_1 (.inst({func7, inst_ex[24:15], func3, inst_ex[11:0]}), .ImmSel(ImmSel), .imm(Imm0));
  control_logic control_logic_1 (
    .CSRWen(CSRWen), .lb(LB), .lh(LH), .sb(SB), .sh(SH), .PCSel(PCSel), .RegWEn(RegWEn), .ImmSel(ImmSel),
    .BrUn(BrUn), .ASel(ASel), .BSel(BSel), .ALUSel(ALUSel), .MemRW(MemRW), .WBSel(WBSel), .CSRSel(CSRSel),
    .inst({func7, inst_ex[24:15], func3, inst_ex[11:0]}), .BrEq(BrEq), .BrLt(BrLt));
  Multiplexer #(.enable("false"), .width(32)) multiplexer_3 (.in0(r1), .in1(pc_ex), .out(ALU_A), .sel(ASel));
  Multiplexer #(.enable("false"), .width(32)) multiplexer_4 (.in0(WRITE_DATA), .in1(Imm0), .out(ALU_B), .sel(BSel));
  alu alu_1 (.Result(WRITE_ADDRESS), .A(ALU_A), .B(ALU_B), .ALUSel(ALUSel));
  regfile regfile_1 (
    .rs1(inst_ex[19:15]), .rs2(inst_ex[24:20]), .rd(inst_ex[11:7]), .Write_Data(wb), .RegWEn(RegWEn),
    .clk(clk), .ra(ra), .sp(sp), .t0(t0), .t1(t1), .t2(t2), .s0(s0), .s1(s1), .a0(a0), .Read_Data_1(r1),
    .Read_Data_2(WRITE_DATA));
  branch_comp branch_comp_1 (.rs1(r1), .rs2(WRITE_DATA), .BrUn(BrUn), .BrEq(BrEq), .BrLt(BrLt));
  Multiplexer #(.enable("false"), .width(4)) multiplexer_5 (
    .in0(4'b1111), .in1(4'b0011), .out(multiplexer_5_out), .sel(SH));
  Multiplexer #(.enable("false"), .width(4)) multiplexer_6 (
    .in0(multiplexer_5_out), .in1(4'b0001), .out(multiplexer_6_out), .sel(SB));
  Multiplexer #(.enable("false"), .width(32)) multiplexer_7 (
    .in0(r1), .in1(Imm0), .out(multiplexer_7_out), .sel(CSRSel));
  Multiplexer #(.enable("false"), .width(4)) multiplexer_8 (
    .in0(4'b0000), .in1(multiplexer_6_out), .out(WRITE_ENABLE), .sel(MemRW));
  assign bit_extender_1_out = {{16{READ_DATA[15]}}, READ_DATA[15:0]};  // Bit_Extender bit_extender_1
  Adder #(.width(32)) adder_2 (.a(pc_ex), .b(32'h4), .out(adder_2_out));  // open: cin, cout
  assign bit_extender_2_out = {{24{READ_DATA[7]}}, READ_DATA[7:0]};  // Bit_Extender bit_extender_2
  Multiplexer #(.enable("false"), .width(32)) multiplexer_9 (
    .in0(READ_DATA), .in1(bit_extender_1_out), .out(multiplexer_9_out), .sel(LH));
  Multiplexer #(.enable("false"), .width(32)) multiplexer_10 (
    .in0(multiplexer_9_out), .in1(bit_extender_2_out), .out(READ_DATA2), .sel(LB));
  Multiplexer #(.enable("false"), .select(2), .width(32)) multiplexer_11 (
    .in0(READ_DATA2), .in1(WRITE_ADDRESS), .in2(adder_2_out), .in3(Imm0), .out(wb), .sel(WBSel));
  csr csr_1 (.CSR_address(12'h51e), .CSR_din(multiplexer_7_out), .CSR_WE(CSRWen), .clk(clk), .tohost(tohost));

  // Other names for the same wires on the sheet: ALU_output[31:0] = WRITE_ADDRESS; opcode[6:0] = inst_ex[6:0];
  //   rd[4:0] = inst_ex[11:7]; inst_ex (some bits) = {func7, func3}; rs1[4:0] = inst_ex[19:15];
  //   rs2[4:0] = inst_ex[24:20]; r2[31:0] = WRITE_DATA

  // Notes on the sheet:
  //   Output to IMEM
  //   IMEM (do **NOT** move this)
  //   Inputs from IMEM
  //   Decode
  //   It is OK to move the PC, RegFile, ALU, MEM, Branch Comp, Imm Gen, and Control Logic to wherever is most convenient for you when constructing your CPU, and to delete this text
  //   Inputs/Outputs for testing. Do **NOT** move these.
  //   Outputs To DMEM
  //   DMEM (do **NOT** move this)
  //   Inputs From DMEM
endmodule
